# Fritzing sketch MysteryMachine2 (saved by Fritzing 0.8.7b)
circuit board: 8.46667cm x 5.64444cm
breadboards: 1

parts:
  Onderdeel1 = Arduino Uno (Rev3)
  RotSwitch1 = female pin header, 6 pins [form="♀ (female)"]
  R1 = Resistor [tolerance=±5% resistance=1k package=THT]
  R2 = Resistor [tolerance=±5% resistance=1k package=THT]
  LED8 = LED - 5mm [color="Red (633nm)" package="5 mm [THT]"]
  LED9 = LED - 5mm [color="Orange (612nm)" package="5 mm [THT]"]
  LED10 = LED - 5mm [color="Yellow (585nm)" package="5 mm [THT]"]
  LED11 = LED - 5mm [color="Green (565nm)" package="5 mm [THT]"]
  LED12 = LED - 5mm [color="Blue (505nm)" package="5 mm [THT]"]
  R3 = Resistor [tolerance=±5% resistance=1k package=THT]
  R4 = Resistor [tolerance=±5% resistance=1k package=THT]
  R5 = Resistor [tolerance=±5% resistance=1k package=THT]
  LED13 = LED - 5mm [color="Red (633nm)" package="5 mm [THT]"]
  RotSwitch2 = female pin header, 6 pins [form="♀ (female)"]
  R11 = Resistor [tolerance=±5% resistance=1k package=THT]
  LED14 = LED - 5mm [color="Orange (612nm)" package="5 mm [THT]"]
  LED15 = LED - 5mm [color="Green (565nm)" package="5 mm [THT]"]
  LED16 = LED - 5mm [color="Yellow (585nm)" package="5 mm [THT]"]
  LED17 = LED - 5mm [color="Blue (505nm)" package="5 mm [THT]"]
  S1 = Pushbutton [package="[THT]"]
  LED18 = LED - 5mm [color="Red (633nm)" package="5 mm [THT]"]
  LED19 = LED - 5mm [color="Green (555nm)" package="5 mm [THT]"]
  LED20 = LED - 5mm [color="Blue (430nm)" package="5 mm [THT]"]
  R23 = Resistor [tolerance=±5% resistance=1k package=THT]
  S2 = Pushbutton [package="[THT]"]
  R24 = Resistor [tolerance=±5% resistance=220 package=THT]
  R25 = Resistor [tolerance=±5% resistance=1k package=THT]
  R26 = Resistor [tolerance=±5% resistance=1k package=THT]
  R27 = Resistor [tolerance=±5% resistance=1k package=THT]
  R28 = Resistor [tolerance=±5% resistance=1k package=THT]
  R29 = Resistor [tolerance=±5% resistance=1k package=THT]
  R30 = Resistor [tolerance=±5% resistance=1k package=THT]
  R31 = Resistor [tolerance=±5% resistance=1k package=THT]
  R32 = Resistor [tolerance=±5% resistance=1k package=THT]
  S3 = Toggle Switch [package=THT]
  S4 = Toggle Switch [package=THT]

nets:
  N1: Onderdeel1.A0, S1.Pin_3, S1.Pin_4, R23.Pin_0
  N2: Onderdeel1.A1, S2.Pin_3, S2.Pin_4, R24.Pin_0
  N3: Onderdeel1.D8, LED18.cathode
  N4: Onderdeel1.D9_PWM, RotSwitch1.pin1, LED8.cathode, R25.Pin_0
  N5: Onderdeel1.D10_PWM/SS, RotSwitch1.pin2, R2.Pin_0, LED9.cathode
  N6: Onderdeel1.D11_PWM/MOSI, RotSwitch1.pin3, LED10.cathode, R3.Pin_0
  N7: Onderdeel1.D12/MISO, RotSwitch1.pin4, LED11.cathode, R5.Pin_0
  N8: Onderdeel1.D13/SCK, RotSwitch1.pin5, LED12.cathode
  N9: Onderdeel1.D0/RX, RotSwitch2.pin3, LED16.cathode, R30.Pin_0
  N10: Onderdeel1.D1/TX, RotSwitch2.pin5, LED17.cathode, R29.Pin_0
  N11: Onderdeel1.D2, RotSwitch2.pin4, LED15.cathode, R28.Pin_0
  N12: Onderdeel1.D3_PWM, RotSwitch2.pin2, LED14.cathode, R27.Pin_0
  N13: Onderdeel1.D4, LED13.cathode, RotSwitch2.pin1, R26.Pin_0
  N14: Onderdeel1.D6_PWM, LED20.cathode
  N15: Onderdeel1.D7, LED19.cathode
  N16: Onderdeel1.5V, RotSwitch1.pin6, RotSwitch2.pin6, S1.Pin_1, S1.Pin_2, S2.Pin_1, S2.Pin_2
  N17: Onderdeel1.GND, S3.COM
  N18: R1.Pin_0, LED8.anode, LED9.anode, LED10.anode, LED11.anode
  N19: R1.Pin_1, R2.Pin_1, R3.Pin_1, R4.Pin_1, R5.Pin_1, R11.Pin_1, R23.Pin_1, R24.Pin_1, R25.Pin_1, R26.Pin_1, R27.Pin_1, R28.Pin_1, R29.Pin_1, R30.Pin_1, R31.Pin_1, R32.Pin_1, S4.COM
  N20: LED12.anode, R4.Pin_0
  N21: LED13.anode, R11.Pin_0, LED14.anode, LED15.anode, LED16.anode
  N22: LED17.anode, R31.Pin_0
  N23: LED18.anode, LED19.anode, LED20.anode, R32.Pin_0
  N24: S3.L1, S4.L1
  N25: S3.L2, S4.L2
